# Fritzing sketch Gree Modbus (saved by Fritzing 0.9.9b)

parts:
  MCU1 = Wemos Lolin32lite
  DS1 = DS18B20 1-Wire Temperature Sensor [part_number=DS18B20]
  RS485_module = RS485 Module (MAX3485)
  Resistor = Resistor [tolerance=±5% resistance=4.7k power=0.25 package=THT]
  DS2 = DS18B20 1-Wire Temperature Sensor [part_number=DS18B20]
  DS3 = DS18B20 1-Wire Temperature Sensor [part_number=DS18B20]
  Relay_module = 4 way omron relay module
  SHT31_or_BME280 = BME280
  240V = Power plug [part_number=240V]
  F2 = Small Fan, based on Fan - Ventilador [package=THT]  # not connected
  part = Small Fan, based on Fan - Ventilador [part_number="Bathroom fan" package=THT]

nets:
  N1: MCU1.pin_8, Relay_module.CH1
  N2: MCU1.pin_9, Relay_module.CH2
  N3: MCU1.pin_10, Relay_module.CH3
  N4: MCU1.pin_11, Relay_module.CH4
  GND: MCU1.pin_13, DS1.GND, RS485_module.GND, DS2.GND, Relay_module.DC-, SHT31_or_BME280.GND
  N5: MCU1.pin_20, DS1.DQ, Resistor.Pin_1, DS2.DQ, DS3.DQ
  N6: MCU1.pin_21, RS485_module.RE
  N7: MCU1.pin_22, RS485_module.DE
  VDD: MCU1.pin_28, DS1.VDD, RS485_module.VCC, Resistor.Pin_0, DS2.VDD, DS3.VDD, Relay_module.DC+
  N8: Relay_module.L1, part.GND
  N9: Relay_module.N1, 240V.GND
  VCC: 240V.VCC, part.5V

notes:
  Gree MODBUS

custom parts:
  Wemos Lolin32lite: Wemos Lolinlite32 wifi and blue tooth board based on the ESP-32 cpu, digital I/Os 19, analog inputs 6, clock 240mhz, Flash 4Mbytes, lipo battery charger (500ma connection broken out on breadboard but not pcb), usb.
  RS485 Module (MAX3485): Commercially available RS485 to RS232 TTL Module
  4 way omron relay module: Low Level 5V 4 Channel Solid State Relay Module SSR G3MB-202P 240V 2A Output with Resistive Fuse.
  BME280: Temperature Humidity Barometric presure Sensor
  Small Fan, based on Fan - Ventilador: Small 2-pin fan, commonly used with single-board computers, 3d-printers, etc. This work is based on a much larger fan, as commonly found in desktop computers
